# Fritzing sketch arduino_webusb_neopixel (saved by Fritzing 0.9.3b)

parts:
  Part1 = Arduino Leonardo (Rev3b)
  NEOPIXEL1 = Neopixel Strip -- Black (60/m) [part_number=1461]

nets:
  N1: Part1.D6_PWM/A7, NEOPIXEL1.DI
  5V: Part1.5V, NEOPIXEL1.+5V
  GND: Part1.GND, NEOPIXEL1.GND

custom parts:
  Neopixel Strip -- Black (60/m): Neopixel Strip, Black, 60 pixels per meter.
